// Logisim project breadboard_computer_simulation.circ as structural Verilog: 18 circuits, main circuit main
module main (
  input  in_1,
  input  in_2,
  input  in_3,
  input  in_4,
  input  in_5,
  input  in_6,
  input  in_7,
  input  in_8,
  input  in_9,
  input  [7:0] in_10,
  input  in_11,
  input  in_12,
  input  in_13,
  input  in_14,
  input  in_15,
  input  in_16,
  input  in_17
);

  wire A0, a0_t, A1, a1_t, A2, a2_t, A3, a3_t, A4, A5, A6, A7, B0, B1, B2, B3, B4, B5, B6, B7, bus0, bus1,
       bus2, bus3, bus4, bus5, bus6, bus7, i0, i1, i2, i3, i4, i5, i6, i7, ic_74189_1_s1_not,
       ic_74189_1_s2_not, ic_74189_1_s3_not, ic_74189_1_s4_not, ic_74189_2_s1_not, ic_74189_2_s2_not,
       ic_74189_2_s3_not, ic_74189_2_s4_not, N0, N1, N2, N3, N4, N5, N6, N7, n74161_1_pin1, n74161_1_pin9,
       n74161_1_pin10, n74161_1_pin11, n74161_1_pin12, n74161_1_pin13, n74161_1_pin14, n74283_1_pin7,
       n74283_1_pin9, not_1_out, not_2_out, not_3_out, not_4_out, not_5_out, not_6_out, not_7_out, not_8_out,
       not_9_out, not_10_out, not_11_out, not_13_out, q0, q1, q2, q3, q4, q5, q6, q7, S0, S1, S2, S3, S4, S5,
       S6, S7;

  not not_1 (not_1_out, in_8);
  IC_74189 ic_74189_1 (
    .S1_not(ic_74189_1_s1_not), .S2_not(ic_74189_1_s2_not), .S3_not(ic_74189_1_s3_not),
    .S4_not(ic_74189_1_s4_not), .D1(bus4), .D2(bus5), .D3(bus6), .D4(bus7), .WE_not(not_1_out), .A0(a0_t),
    .A1(a1_t), .A2(a2_t), .A3(a3_t));
  IC_74189 ic_74189_2 (
    .S1_not(ic_74189_2_s1_not), .S2_not(ic_74189_2_s2_not), .S3_not(ic_74189_2_s3_not),
    .S4_not(ic_74189_2_s4_not), .D1(bus0), .D2(bus1), .D3(bus2), .D4(bus3), .WE_not(not_1_out), .A0(a0_t),
    .A1(a1_t), .A2(a2_t), .A3(a3_t));
  IC_74173_quad_D_type_flip_flop ic_74173_quad_d_type_flip_flop_1 (
    .Q0(i4), .Q1(i5), .Q2(i6), .Q3(i7), .E1_active_low(not_2_out), .E2_active_low(not_2_out), .CP(in_1),
    .MR(1'b0), .OE1_active_low(1'b0), .D0(bus7), .D1(bus6), .D2(bus5), .OE2_active_low(1'b0), .D3(bus4));
  _7404 #(.ShowInternalStructure("true")) u_7404_1 (
    .pin1(ic_74189_2_s2_not), .pin2(q1), .pin3(ic_74189_2_s1_not), .pin4(q0), .pin13(ic_74189_2_s3_not),
    .pin12(q2), .pin11(ic_74189_2_s4_not), .pin10(q3));  // open: pin5, pin6, pin9, pin8
  LED led_1 (.in(q7));
  LED led_2 (.in(q6));
  LED led_3 (.in(q5));
  not not_2 (not_2_out, in_12);
  IC_74173_quad_D_type_flip_flop ic_74173_quad_d_type_flip_flop_2 (
    .Q0(i0), .Q1(i1), .Q2(i2), .Q3(i3), .E1_active_low(not_2_out), .E2_active_low(not_2_out), .CP(in_1),
    .MR(1'b0), .OE1_active_low(1'b0), .D0(bus3), .D1(bus2), .D2(bus1), .OE2_active_low(1'b0), .D3(bus0));
  LED led_4 (.in(i7));
  _7404 #(.ShowInternalStructure("true")) u_7404_2 (
    .pin1(ic_74189_1_s2_not), .pin2(q5), .pin3(ic_74189_1_s1_not), .pin4(q4), .pin13(ic_74189_1_s3_not),
    .pin12(q6), .pin11(ic_74189_1_s4_not), .pin10(q7));  // open: pin5, pin6, pin9, pin8
  LED led_5 (.in(q4));
  LED led_6 (.in(q3));
  LED led_7 (.in(q2));
  LED led_8 (.in(q1));
  LED led_9 (.in(a3_t));
  LED led_10 (.in(a2_t));
  LED led_11 (.in(i6));
  LED led_12 (.in(i5));
  LED led_13 (.in(i4));
  not not_3 (not_3_out, in_9);
  LED led_14 (.in(q0));
  not not_4 (not_4_out, in_11);
  LED led_15 (.in(a1_t));
  LED led_16 (.in(a0_t));
  LED led_17 (.in(i3));
  LED led_18 (.in(i2));
  LED led_19 (.in(i1));
  LED led_20 (.in(i0));
  IC_74245_octal_transceiver_down ic_74245_octal_transceiver_down_1 (
    .A1(bus0), .A2(bus1), .A3(bus2), .A4(bus3), .A5(bus4), .A6(bus5), .A7(bus6), .A8(bus7),
    .OE_active_low(not_5_out), .B1(i0), .B2(i1), .B3(i2), .B4(i3), .B5(1'b0), .B6(1'b0), .B7(1'b0),
    .B8(1'b0), .DIR(1'b0));
  not not_5 (not_5_out, in_13);
  IC_74173_quad_D_type_flip_flop ic_74173_quad_d_type_flip_flop_3 (
    .Q0(a0_t), .Q1(a1_t), .Q2(a2_t), .Q3(a3_t), .E1_active_low(not_4_out), .E2_active_low(not_4_out),
    .CP(in_1), .MR(1'b0), .OE1_active_low(1'b0), .D0(bus0), .D1(bus1), .D2(bus2), .OE2_active_low(1'b0),
    .D3(bus3));
  IC_74245_octal_transceiver_down ic_74245_octal_transceiver_down_2 (
    .A1(bus0), .A2(bus1), .A3(bus2), .A4(bus3), .A5(bus4), .A6(bus5), .A7(bus6), .A8(bus7),
    .OE_active_low(not_3_out), .B1(q0), .B2(q1), .B3(q2), .B4(q3), .B5(q4), .B6(q5), .B7(q6), .B8(q7),
    .DIR(1'b0));
  not not_6 (not_6_out, in_5);
  LED led_21 (.in(bus7));
  LED led_22 (.in(bus6));
  LED led_23 (.in(bus5));
  LED led_24 (.in(bus4));
  not not_7 (not_7_out, in_14);
  not not_8 (not_8_out, in_16);
  LED led_25 (.in(bus3));
  LED led_26 (.in(bus2));
  LED led_27 (.in(bus1));
  LED led_28 (.in(bus0));
  IC_74245_octal_transceiver_up ic_74245_octal_transceiver_up_1 (
    .B1(bus7), .B2(bus6), .B3(bus5), .B4(bus4), .B5(bus3), .B6(bus2), .B7(bus1), .B8(bus0),
    .OE_active_low(not_6_out), .A1(in_10[7]), .A2(in_10[6]), .A3(in_10[5]), .A4(in_10[4]), .A5(in_10[3]),
    .DIR(1'b1), .A6(in_10[2]), .A7(in_10[1]), .A8(in_10[0]));
  LED led_29 (.in(S7));
  LED led_30 (.in(S6));
  LED led_31 (.in(S5));
  LED led_32 (.in(S4));
  LED led_33 (.in(S3));
  LED led_34 (.in(S2));
  LED led_35 (.in(S1));
  _74283 #(.ShowInternalStructure("true")) u_74283_1 (
    .pin1(S5), .pin2(N5), .pin3(A5), .pin4(S4), .pin5(A4), .pin6(N4), .pin7(n74283_1_pin7), .pin15(N6),
    .pin14(A6), .pin13(S6), .pin12(A7), .pin11(N7), .pin10(S7), .pin9(n74283_1_pin9));
  IC_74245_octal_transceiver_up ic_74245_octal_transceiver_up_2 (
    .B1(bus7), .B2(bus6), .B3(bus5), .B4(bus4), .B5(bus3), .B6(bus2), .B7(bus1), .B8(bus0),
    .OE_active_low(not_7_out), .A1(S7), .A2(S6), .A3(S5), .A4(S4), .A5(S3), .DIR(1'b1), .A6(S2), .A7(S1),
    .A8(S0));
  LED led_36 (.in(S0));
  LED led_37 (.in(B7));
  LED led_38 (.in(B6));
  IC_74245_octal_transceiver_down ic_74245_octal_transceiver_down_3 (
    .A1(bus7), .A2(bus6), .A3(bus5), .A4(bus4), .A5(bus3), .A6(bus2), .A7(bus1), .A8(bus0),
    .OE_active_low(not_8_out), .B1(B7), .B2(B6), .B3(B5), .B4(B4), .B5(B3), .B6(B2), .B7(B1), .B8(B0),
    .DIR(1'b0));
  not not_9 (not_9_out, in_4);
  not not_10 (not_10_out, in_6);
  LED led_39 (.in(B5));
  LED led_40 (.in(B4));
  LED led_41 (.in(B3));
  LED led_42 (.in(B2));
  LED overflow (.in(n74283_1_pin9));
  _7486 #(.ShowInternalStructure("true")) u_7486_1 (
    .pin1(in_15), .pin2(B4), .pin3(N4), .pin4(in_15), .pin5(B5), .pin6(N5), .pin13(B7), .pin12(in_15),
    .pin11(N7), .pin10(B6), .pin9(in_15), .pin8(N6));
  LED led_43 (.in(B1));
  LED led_44 (.in(B0));
  IC_74173_quad_D_type_flip_flop ic_74173_quad_d_type_flip_flop_4 (
    .Q0(B4), .Q1(B5), .Q2(B6), .Q3(B7), .E1_active_low(not_11_out), .E2_active_low(not_11_out), .CP(in_1),
    .MR(1'b0), .OE1_active_low(1'b0), .D0(bus4), .D1(bus5), .D2(bus6), .OE2_active_low(1'b0), .D3(bus7));
  IC_74245_octal_transceiver_down ic_74245_octal_transceiver_down_4 (
    .A1(bus7), .A2(bus6), .A3(bus5), .A4(bus4), .A5(bus3), .A6(bus2), .A7(bus1), .A8(bus0),
    .OE_active_low(not_9_out), .B1(1'b0), .B2(1'b0), .B3(1'b0), .B4(1'b0), .B5(n74161_1_pin11),
    .B6(n74161_1_pin12), .B7(n74161_1_pin13), .B8(n74161_1_pin14), .DIR(1'b0));
  IC_74245_octal_transceiver_up ic_74245_octal_transceiver_up_3 (
    .B1(bus7), .B2(bus6), .B3(bus5), .B4(bus4), .B5(bus3), .B6(bus2), .B7(bus1), .B8(bus0),
    .OE_active_low(not_10_out), .A1(A7), .A2(A6), .A3(A5), .A4(A4), .A5(A3), .DIR(1'b1), .A6(A2), .A7(A1),
    .A8(A0));
  LED led_45 (.in(n74161_1_pin11));
  LED led_46 (.in(n74161_1_pin12));
  LED led_47 (.in(n74161_1_pin13));
  LED led_48 (.in(n74161_1_pin14));
  LED led_49 (.in(A7));
  LED led_50 (.in(A6));
  LED led_51 (.in(A5));
  LED led_52 (.in(A4));
  _74283 #(.ShowInternalStructure("true")) u_74283_2 (
    .pin1(S1), .pin2(N1), .pin3(A1), .pin4(S0), .pin5(A0), .pin6(N0), .pin7(in_15), .pin15(N2), .pin14(A2),
    .pin13(S2), .pin12(A3), .pin11(N3), .pin10(S3), .pin9(n74283_1_pin7));
  IC_74173_quad_D_type_flip_flop ic_74173_quad_d_type_flip_flop_5 (
    .Q0(B0), .Q1(B1), .Q2(B2), .Q3(B3), .E1_active_low(not_11_out), .E2_active_low(not_11_out), .CP(in_1),
    .MR(1'b0), .OE1_active_low(1'b0), .D0(bus0), .D1(bus1), .D2(bus2), .OE2_active_low(1'b0), .D3(bus3));
  _74161 #(.ShowInternalStructure("true")) u_74161_1 (
    .pin1(n74161_1_pin1), .pin2(in_1), .pin3(bus3), .pin4(bus2), .pin5(bus1), .pin6(bus0), .pin7(in_3),
    .pin14(n74161_1_pin14), .pin13(n74161_1_pin13), .pin12(n74161_1_pin12), .pin11(n74161_1_pin11),
    .pin10(n74161_1_pin10), .pin9(n74161_1_pin9));  // open: pin15
  LED led_53 (.in(A3));
  LED led_54 (.in(A2));
  LED led_55 (.in(A1));
  LED led_56 (.in(A0));
  _7486 #(.ShowInternalStructure("true")) u_7486_2 (
    .pin1(in_15), .pin2(B0), .pin3(N0), .pin4(in_15), .pin5(B1), .pin6(N1), .pin13(B3), .pin12(in_15),
    .pin11(N3), .pin10(B2), .pin9(in_15), .pin8(N2));
  not not_11 (not_11_out, in_17);
  not not_12 (n74161_1_pin9, in_2);
  IC_74173_quad_D_type_flip_flop ic_74173_quad_d_type_flip_flop_6 (
    .Q0(A7), .Q1(A6), .Q2(A5), .Q3(A4), .E1_active_low(not_13_out), .E2_active_low(not_13_out), .CP(in_1),
    .MR(1'b0), .OE1_active_low(1'b0), .D0(bus7), .D1(bus6), .D2(bus5), .OE2_active_low(1'b0), .D3(bus4));
  not not_13 (not_13_out, in_7);
  IC_74173_quad_D_type_flip_flop ic_74173_quad_d_type_flip_flop_7 (
    .Q0(A3), .Q1(A2), .Q2(A1), .Q3(A0), .E1_active_low(not_13_out), .E2_active_low(not_13_out), .CP(in_1),
    .MR(1'b0), .OE1_active_low(1'b0), .D0(bus3), .D1(bus2), .D2(bus1), .OE2_active_low(1'b0), .D3(bus0));
  // also tied to VCC on the sheet: {n74161_1_pin1, n74161_1_pin10}

  // Other names for the same wires on the sheet: clk = in_1; ctrl_ALU_out = in_14; ctrl_ALU_sub = in_15;
  //   ctrl_IR_in = in_12; ctrl_IR_out = in_13; ctrl_MAR_in = in_11; ctrl_PC_en = in_3; ctrl_PC_load = in_2;
  //   ctrl_PC_out = in_4; ctrl_Ra_in = in_7; ctrl_Ra_out = in_6; ctrl_RAM_in = in_8; ctrl_RAM_out = in_9;
  //   ctrl_Rb_in = in_17; ctrl_Rb_out = in_16

  // Notes on the sheet:
  //   RAM
  //   INSTRUCTION REGISTER
  //   MAR
  //   SYSTEM BUS
  //   B REGISTER
  //   PROGRAM COUNTER
  //   A REGISTER
  //   ALU [a0 .. a7] is register A, [b0 .. b7] is register B, [n0 .. n7] is negated content of register B,  [s0 .. s7] is result
endmodule

module system_bus (
  input  in_1,
  input  [7:0] in_2
);

  wire bus0, bus1, bus2, bus3, bus4, bus5, bus6, bus7, not_1_out;

  not not_1 (not_1_out, in_1);
  LED led_1 (.in(bus6));
  LED led_2 (.in(bus5));
  LED led_3 (.in(bus4));
  LED led_4 (.in(bus7));
  LED led_5 (.in(bus3));
  LED led_6 (.in(bus2));
  LED led_7 (.in(bus1));
  LED led_8 (.in(bus0));
  IC_74245_octal_transceiver_up ic_74245_octal_transceiver_up_1 (
    .B1(bus7), .B2(bus6), .B3(bus5), .B4(bus4), .B5(bus3), .B6(bus2), .B7(bus1), .B8(bus0),
    .OE_active_low(not_1_out), .A1(in_2[7]), .A2(in_2[6]), .A3(in_2[5]), .A4(in_2[4]), .A5(in_2[3]),
    .DIR(1'b1), .A6(in_2[2]), .A7(in_2[1]), .A8(in_2[0]));

  // Notes on the sheet:
  //   SYSTEM BUS
endmodule

module program_counter (
  input  in_1,
  input  in_2,
  input  in_3,
  input  in_4,
  input  in_5,
  input  [7:0] in_6
);

  wire bus0, bus1, bus2, bus3, bus4, bus5, bus6, bus7, n74161_1_pin1, n74161_1_pin9, n74161_1_pin10,
       n74161_1_pin11, n74161_1_pin12, n74161_1_pin13, n74161_1_pin14, not_1_out, not_2_out;

  not not_1 (not_1_out, in_5);
  LED led_1 (.in(bus6));
  LED led_2 (.in(bus5));
  LED led_3 (.in(bus4));
  LED led_4 (.in(bus7));
  not not_2 (not_2_out, in_3);
  LED led_5 (.in(bus3));
  LED led_6 (.in(bus2));
  LED led_7 (.in(bus1));
  LED led_8 (.in(bus0));
  IC_74245_octal_transceiver_up ic_74245_octal_transceiver_up_1 (
    .B1(bus7), .B2(bus6), .B3(bus5), .B4(bus4), .B5(bus3), .B6(bus2), .B7(bus1), .B8(bus0),
    .OE_active_low(not_1_out), .A1(in_6[7]), .A2(in_6[6]), .A3(in_6[5]), .A4(in_6[4]), .A5(in_6[3]),
    .DIR(1'b1), .A6(in_6[2]), .A7(in_6[1]), .A8(in_6[0]));
  IC_74245_octal_transceiver_down ic_74245_octal_transceiver_down_1 (
    .A1(bus7), .A2(bus6), .A3(bus5), .A4(bus4), .A5(bus3), .A6(bus2), .A7(bus1), .A8(bus0),
    .OE_active_low(not_2_out), .B1(1'b0), .B2(1'b0), .B3(1'b0), .B4(1'b0), .B5(n74161_1_pin11),
    .B6(n74161_1_pin12), .B7(n74161_1_pin13), .B8(n74161_1_pin14), .DIR(1'b0));
  LED led_9 (.in(n74161_1_pin11));
  LED led_10 (.in(n74161_1_pin12));
  LED led_11 (.in(n74161_1_pin13));
  LED led_12 (.in(n74161_1_pin14));
  _74161 #(.ShowInternalStructure("true")) u_74161_1 (
    .pin1(n74161_1_pin1), .pin2(in_4), .pin3(bus3), .pin4(bus2), .pin5(bus1), .pin6(bus0), .pin7(in_2),
    .pin14(n74161_1_pin14), .pin13(n74161_1_pin13), .pin12(n74161_1_pin12), .pin11(n74161_1_pin11),
    .pin10(n74161_1_pin10), .pin9(n74161_1_pin9));  // open: pin15
  not not_3 (n74161_1_pin9, in_1);
  // also tied to VCC on the sheet: {n74161_1_pin1, n74161_1_pin10}

  // Other names for the same wires on the sheet: clk = in_4; ctrl_PC_en = in_2; ctrl_PC_load = in_1;
  //   ctrl_PC_out = in_3

  // Notes on the sheet:
  //   SYSTEM BUS
  //   PROGRAM COUNTER
endmodule

module A_Register (
  input  in_1,
  input  in_2,
  input  in_3,
  input  in_4,
  input  [7:0] in_5
);

  wire A0, A1, A2, A3, A4, A5, A6, A7, bus0, bus1, bus2, bus3, bus4, bus5, bus6, bus7, not_1_out, not_2_out,
       not_3_out;

  not not_1 (not_1_out, in_4);
  LED led_1 (.in(bus6));
  LED led_2 (.in(bus5));
  LED led_3 (.in(bus4));
  LED led_4 (.in(bus7));
  not not_2 (not_2_out, in_1);
  LED led_5 (.in(bus3));
  LED led_6 (.in(bus2));
  LED led_7 (.in(bus1));
  LED led_8 (.in(bus0));
  IC_74245_octal_transceiver_up ic_74245_octal_transceiver_up_1 (
    .B1(bus7), .B2(bus6), .B3(bus5), .B4(bus4), .B5(bus3), .B6(bus2), .B7(bus1), .B8(bus0),
    .OE_active_low(not_1_out), .A1(in_5[7]), .A2(in_5[6]), .A3(in_5[5]), .A4(in_5[4]), .A5(in_5[3]),
    .DIR(1'b1), .A6(in_5[2]), .A7(in_5[1]), .A8(in_5[0]));
  IC_74245_octal_transceiver_up ic_74245_octal_transceiver_up_2 (
    .B1(bus7), .B2(bus6), .B3(bus5), .B4(bus4), .B5(bus3), .B6(bus2), .B7(bus1), .B8(bus0),
    .OE_active_low(not_2_out), .A1(A7), .A2(A6), .A3(A5), .A4(A4), .A5(A3), .DIR(1'b1), .A6(A2), .A7(A1),
    .A8(A0));
  LED led_9 (.in(A7));
  LED led_10 (.in(A6));
  LED led_11 (.in(A5));
  LED led_12 (.in(A4));
  LED led_13 (.in(A3));
  LED led_14 (.in(A2));
  LED led_15 (.in(A1));
  LED led_16 (.in(A0));
  IC_74173_quad_D_type_flip_flop ic_74173_quad_d_type_flip_flop_1 (
    .Q0(A7), .Q1(A6), .Q2(A5), .Q3(A4), .E1_active_low(not_3_out), .E2_active_low(not_3_out), .CP(in_3),
    .MR(1'b0), .OE1_active_low(1'b0), .D0(bus7), .D1(bus6), .D2(bus5), .OE2_active_low(1'b0), .D3(bus4));
  not not_3 (not_3_out, in_2);
  IC_74173_quad_D_type_flip_flop ic_74173_quad_d_type_flip_flop_2 (
    .Q0(A3), .Q1(A2), .Q2(A1), .Q3(A0), .E1_active_low(not_3_out), .E2_active_low(not_3_out), .CP(in_3),
    .MR(1'b0), .OE1_active_low(1'b0), .D0(bus3), .D1(bus2), .D2(bus1), .OE2_active_low(1'b0), .D3(bus0));

  // Other names for the same wires on the sheet: clk = in_3; ctrl_Ra_in = in_2; ctrl_Ra_out = in_1

  // Notes on the sheet:
  //   SYSTEM BUS
  //   A REGISTER
endmodule

module B_Register (
  input  in_1,
  input  in_2,
  input  in_3,
  input  in_4,
  input  [7:0] in_5
);

  wire B0, B1, B2, B3, B4, B5, B6, B7, bus0, bus1, bus2, bus3, bus4, bus5, bus6, bus7, not_1_out, not_2_out,
       not_3_out;

  not not_1 (not_1_out, in_4);
  LED led_1 (.in(bus6));
  LED led_2 (.in(bus5));
  LED led_3 (.in(bus4));
  LED led_4 (.in(bus7));
  not not_2 (not_2_out, in_1);
  LED led_5 (.in(bus3));
  LED led_6 (.in(bus2));
  LED led_7 (.in(bus1));
  LED led_8 (.in(bus0));
  IC_74245_octal_transceiver_up ic_74245_octal_transceiver_up_1 (
    .B1(bus7), .B2(bus6), .B3(bus5), .B4(bus4), .B5(bus3), .B6(bus2), .B7(bus1), .B8(bus0),
    .OE_active_low(not_1_out), .A1(in_5[7]), .A2(in_5[6]), .A3(in_5[5]), .A4(in_5[4]), .A5(in_5[3]),
    .DIR(1'b1), .A6(in_5[2]), .A7(in_5[1]), .A8(in_5[0]));
  LED led_9 (.in(B7));
  IC_74245_octal_transceiver_down ic_74245_octal_transceiver_down_1 (
    .A1(bus7), .A2(bus6), .A3(bus5), .A4(bus4), .A5(bus3), .A6(bus2), .A7(bus1), .A8(bus0),
    .OE_active_low(not_2_out), .B1(B7), .B2(B6), .B3(B5), .B4(B4), .B5(B3), .B6(B2), .B7(B1), .B8(B0),
    .DIR(1'b0));
  LED led_10 (.in(B6));
  LED led_11 (.in(B5));
  LED led_12 (.in(B4));
  LED led_13 (.in(B3));
  LED led_14 (.in(B2));
  LED led_15 (.in(B1));
  LED led_16 (.in(B0));
  IC_74173_quad_D_type_flip_flop ic_74173_quad_d_type_flip_flop_1 (
    .Q0(B4), .Q1(B5), .Q2(B6), .Q3(B7), .E1_active_low(not_3_out), .E2_active_low(not_3_out), .CP(in_3),
    .MR(1'b0), .OE1_active_low(1'b0), .D0(bus4), .D1(bus5), .D2(bus6), .OE2_active_low(1'b0), .D3(bus7));
  IC_74173_quad_D_type_flip_flop ic_74173_quad_d_type_flip_flop_2 (
    .Q0(B0), .Q1(B1), .Q2(B2), .Q3(B3), .E1_active_low(not_3_out), .E2_active_low(not_3_out), .CP(in_3),
    .MR(1'b0), .OE1_active_low(1'b0), .D0(bus0), .D1(bus1), .D2(bus2), .OE2_active_low(1'b0), .D3(bus3));
  not not_3 (not_3_out, in_2);

  // Other names for the same wires on the sheet: clk = in_3; ctrl_Rb_in = in_2; ctrl_Rb_out = in_1

  // Notes on the sheet:
  //   SYSTEM BUS
  //   B REGISTER
endmodule

module ALU (
  input  in_1,
  input  in_2,
  input  in_3,
  input  [7:0] in_4,
  input  [7:0] in_5,
  input  [7:0] in_6
);

  wire bus0, bus1, bus2, bus3, bus4, bus5, bus6, bus7, N0, N1, N2, N3, N4, N5, N6, N7, n74283_1_pin7,
       n74283_1_pin9, not_1_out, not_2_out, S0, S1, S2, S3, S4, S5, S6, S7;

  not not_1 (not_1_out, in_2);
  LED led_1 (.in(S7));
  LED led_2 (.in(S6));
  LED led_3 (.in(S5));
  LED led_4 (.in(S4));
  LED led_5 (.in(S3));
  LED led_6 (.in(S2));
  _74283 #(.ShowInternalStructure("true")) u_74283_1 (
    .pin1(S5), .pin2(N5), .pin3(in_5[5]), .pin4(S4), .pin5(in_5[4]), .pin6(N4), .pin7(n74283_1_pin7),
    .pin15(N6), .pin14(in_5[6]), .pin13(S6), .pin12(in_5[7]), .pin11(N7), .pin10(S7), .pin9(n74283_1_pin9));
  IC_74245_octal_transceiver_up ic_74245_octal_transceiver_up_1 (
    .B1(bus7), .B2(bus6), .B3(bus5), .B4(bus4), .B5(bus3), .B6(bus2), .B7(bus1), .B8(bus0),
    .OE_active_low(not_1_out), .A1(S7), .A2(S6), .A3(S5), .A4(S4), .A5(S3), .DIR(1'b1), .A6(S2), .A7(S1),
    .A8(S0));
  LED led_7 (.in(S1));
  LED led_8 (.in(S0));
  LED overflow (.in(n74283_1_pin9));
  _7486 #(.ShowInternalStructure("true")) u_7486_1 (
    .pin1(in_3), .pin2(in_6[4]), .pin3(N4), .pin4(in_3), .pin5(in_6[5]), .pin6(N5), .pin13(in_6[7]),
    .pin12(in_3), .pin11(N7), .pin10(in_6[6]), .pin9(in_3), .pin8(N6));
  _74283 #(.ShowInternalStructure("true")) u_74283_2 (
    .pin1(S1), .pin2(N1), .pin3(in_5[1]), .pin4(S0), .pin5(in_5[0]), .pin6(N0), .pin7(in_3), .pin15(N2),
    .pin14(in_5[2]), .pin13(S2), .pin12(in_5[3]), .pin11(N3), .pin10(S3), .pin9(n74283_1_pin7));
  _7486 #(.ShowInternalStructure("true")) u_7486_2 (
    .pin1(in_3), .pin2(in_6[0]), .pin3(N0), .pin4(in_3), .pin5(in_6[1]), .pin6(N1), .pin13(in_6[3]),
    .pin12(in_3), .pin11(N3), .pin10(in_6[2]), .pin9(in_3), .pin8(N2));
  LED led_9 (.in(bus7));
  LED led_10 (.in(bus6));
  LED led_11 (.in(bus5));
  not not_2 (not_2_out, in_1);
  LED led_12 (.in(bus4));
  LED led_13 (.in(bus3));
  LED led_14 (.in(bus2));
  LED led_15 (.in(bus1));
  LED led_16 (.in(bus0));
  IC_74245_octal_transceiver_up ic_74245_octal_transceiver_up_2 (
    .B1(bus7), .B2(bus6), .B3(bus5), .B4(bus4), .B5(bus3), .B6(bus2), .B7(bus1), .B8(bus0),
    .OE_active_low(not_2_out), .A1(in_4[7]), .A2(in_4[6]), .A3(in_4[5]), .A4(in_4[4]), .A5(in_4[3]),
    .DIR(1'b1), .A6(in_4[2]), .A7(in_4[1]), .A8(in_4[0]));

  // Other names for the same wires on the sheet: ctrl_ALU_out = in_2; ctrl_ALU_sub = in_3; A0 = in_5[0]; A1 = in_5[1];
  //   A2 = in_5[2]; A3 = in_5[3]; A4 = in_5[4]; A5 = in_5[5]; A6 = in_5[6]; A7 = in_5[7]; B0 = in_6[0]; B1 = in_6[1];
  //   B2 = in_6[2]; B3 = in_6[3]; B4 = in_6[4]; B5 = in_6[5]; B6 = in_6[6]; B7 = in_6[7]

  // Notes on the sheet:
  //   ALU [a0 .. a7] is register A, [b0 .. b7] is register B, [n0 .. n7] is negated content of register B,  [s0 .. s7] is result
  //   SYSTEM BUS
endmodule

module system_RAM (
  input  in_1,
  input  in_2,
  input  in_3,
  input  [7:0] in_4,
  input  in_5,
  input  in_6,
  input  in_7,
  input  in_8
);

  wire bus0, bus1, bus2, bus3, bus4, bus5, bus6, bus7, ic_74189_1_s1_not, ic_74189_1_s2_not,
       ic_74189_1_s3_not, ic_74189_1_s4_not, ic_74189_2_s1_not, ic_74189_2_s2_not, ic_74189_2_s3_not,
       ic_74189_2_s4_not, not_1_out, not_2_out, not_3_out, q0, q1, q2, q3, q4, q5, q6, q7;

  not not_1 (not_1_out, in_2);
  IC_74189 ic_74189_1 (
    .S1_not(ic_74189_1_s1_not), .S2_not(ic_74189_1_s2_not), .S3_not(ic_74189_1_s3_not),
    .S4_not(ic_74189_1_s4_not), .D1(bus4), .D2(bus5), .D3(bus6), .D4(bus7), .WE_not(not_1_out), .A0(in_5),
    .A1(in_6), .A2(in_7), .A3(in_8));
  IC_74189 ic_74189_2 (
    .S1_not(ic_74189_2_s1_not), .S2_not(ic_74189_2_s2_not), .S3_not(ic_74189_2_s3_not),
    .S4_not(ic_74189_2_s4_not), .D1(bus0), .D2(bus1), .D3(bus2), .D4(bus3), .WE_not(not_1_out), .A0(in_5),
    .A1(in_6), .A2(in_7), .A3(in_8));
  _7404 #(.ShowInternalStructure("true")) u_7404_1 (
    .pin1(ic_74189_2_s2_not), .pin2(q1), .pin3(ic_74189_2_s1_not), .pin4(q0), .pin13(ic_74189_2_s3_not),
    .pin12(q2), .pin11(ic_74189_2_s4_not), .pin10(q3));  // open: pin5, pin6, pin9, pin8
  LED led_1 (.in(q7));
  LED led_2 (.in(q6));
  LED led_3 (.in(q5));
  _7404 #(.ShowInternalStructure("true")) u_7404_2 (
    .pin1(ic_74189_1_s2_not), .pin2(q5), .pin3(ic_74189_1_s1_not), .pin4(q4), .pin13(ic_74189_1_s3_not),
    .pin12(q6), .pin11(ic_74189_1_s4_not), .pin10(q7));  // open: pin5, pin6, pin9, pin8
  LED led_4 (.in(q4));
  LED led_5 (.in(q3));
  LED led_6 (.in(q2));
  LED led_7 (.in(q1));
  not not_2 (not_2_out, in_3);
  LED led_8 (.in(q0));
  IC_74245_octal_transceiver_down ic_74245_octal_transceiver_down_1 (
    .A1(bus0), .A2(bus1), .A3(bus2), .A4(bus3), .A5(bus4), .A6(bus5), .A7(bus6), .A8(bus7),
    .OE_active_low(not_2_out), .B1(q0), .B2(q1), .B3(q2), .B4(q3), .B5(q4), .B6(q5), .B7(q6), .B8(q7),
    .DIR(1'b0));
  LED led_9 (.in(bus7));
  LED led_10 (.in(bus6));
  LED led_11 (.in(bus5));
  not not_3 (not_3_out, in_1);
  LED led_12 (.in(bus4));
  LED led_13 (.in(bus3));
  LED led_14 (.in(bus2));
  LED led_15 (.in(bus1));
  LED led_16 (.in(bus0));
  IC_74245_octal_transceiver_up ic_74245_octal_transceiver_up_1 (
    .B1(bus7), .B2(bus6), .B3(bus5), .B4(bus4), .B5(bus3), .B6(bus2), .B7(bus1), .B8(bus0),
    .OE_active_low(not_3_out), .A1(in_4[7]), .A2(in_4[6]), .A3(in_4[5]), .A4(in_4[4]), .A5(in_4[3]),
    .DIR(1'b1), .A6(in_4[2]), .A7(in_4[1]), .A8(in_4[0]));

  // Other names for the same wires on the sheet: a0 = in_5; a1 = in_6; a2 = in_7; a3 = in_8; ctrl_RAM_in = in_2;
  //   ctrl_RAM_out = in_3

  // Notes on the sheet:
  //   RAM
  //   SYSTEM BUS
endmodule

module MAR (
  input  in_1,
  input  in_2,
  input  in_3,
  input  [7:0] in_4
);

  wire a0, a1, a2, a3, bus0, bus1, bus2, bus3, bus4, bus5, bus6, bus7, not_1_out, not_2_out;

  LED led_1 (.in(a3));
  LED led_2 (.in(a2));
  LED led_3 (.in(a1));
  not not_1 (not_1_out, in_1);
  LED led_4 (.in(a0));
  IC_74173_quad_D_type_flip_flop ic_74173_quad_d_type_flip_flop_1 (
    .Q0(a0), .Q1(a1), .Q2(a2), .Q3(a3), .E1_active_low(not_1_out), .E2_active_low(not_1_out), .CP(in_2),
    .MR(1'b0), .OE1_active_low(1'b0), .D0(bus0), .D1(bus1), .D2(bus2), .OE2_active_low(1'b0), .D3(bus3));
  LED led_5 (.in(bus7));
  not not_2 (not_2_out, in_3);
  LED led_6 (.in(bus6));
  LED led_7 (.in(bus5));
  LED led_8 (.in(bus4));
  LED led_9 (.in(bus3));
  LED led_10 (.in(bus2));
  LED led_11 (.in(bus1));
  LED led_12 (.in(bus0));
  IC_74245_octal_transceiver_up ic_74245_octal_transceiver_up_1 (
    .B1(bus7), .B2(bus6), .B3(bus5), .B4(bus4), .B5(bus3), .B6(bus2), .B7(bus1), .B8(bus0),
    .OE_active_low(not_2_out), .A1(in_4[7]), .A2(in_4[6]), .A3(in_4[5]), .A4(in_4[4]), .A5(in_4[3]),
    .DIR(1'b1), .A6(in_4[2]), .A7(in_4[1]), .A8(in_4[0]));

  // Other names for the same wires on the sheet: clk = in_2; ctrl_MAR_in = in_1

  // Notes on the sheet:
  //   MAR
  //   SYSTEM BUS
endmodule

module IR (
  input  in_1,
  input  in_2,
  input  in_3,
  input  in_4,
  input  [7:0] in_5
);

  wire bus0, bus1, bus2, bus3, bus4, bus5, bus6, bus7, i0, i1, i2, i3, i4, i5, i6, i7, not_1_out, not_2_out,
       not_3_out;

  LED led_1 (.in(bus7));
  LED led_2 (.in(bus6));
  LED led_3 (.in(bus5));
  not not_1 (not_1_out, in_4);
  IC_74173_quad_D_type_flip_flop ic_74173_quad_d_type_flip_flop_1 (
    .Q0(i4), .Q1(i5), .Q2(i6), .Q3(i7), .E1_active_low(not_2_out), .E2_active_low(not_2_out), .CP(in_3),
    .MR(1'b0), .OE1_active_low(1'b0), .D0(bus7), .D1(bus6), .D2(bus5), .OE2_active_low(1'b0), .D3(bus4));
  LED led_4 (.in(bus4));
  LED led_5 (.in(bus3));
  LED led_6 (.in(bus2));
  LED led_7 (.in(bus1));
  LED led_8 (.in(bus0));
  IC_74245_octal_transceiver_up ic_74245_octal_transceiver_up_1 (
    .B1(bus7), .B2(bus6), .B3(bus5), .B4(bus4), .B5(bus3), .B6(bus2), .B7(bus1), .B8(bus0),
    .OE_active_low(not_1_out), .A1(in_5[7]), .A2(in_5[6]), .A3(in_5[5]), .A4(in_5[4]), .A5(in_5[3]),
    .DIR(1'b1), .A6(in_5[2]), .A7(in_5[1]), .A8(in_5[0]));
  not not_2 (not_2_out, in_1);
  IC_74173_quad_D_type_flip_flop ic_74173_quad_d_type_flip_flop_2 (
    .Q0(i0), .Q1(i1), .Q2(i2), .Q3(i3), .E1_active_low(not_2_out), .E2_active_low(not_2_out), .CP(in_3),
    .MR(1'b0), .OE1_active_low(1'b0), .D0(bus3), .D1(bus2), .D2(bus1), .OE2_active_low(1'b0), .D3(bus0));
  LED led_9 (.in(i7));
  LED led_10 (.in(i6));
  LED led_11 (.in(i5));
  LED led_12 (.in(i4));
  LED led_13 (.in(i3));
  LED led_14 (.in(i2));
  LED led_15 (.in(i1));
  LED led_16 (.in(i0));
  IC_74245_octal_transceiver_down ic_74245_octal_transceiver_down_1 (
    .A1(bus0), .A2(bus1), .A3(bus2), .A4(bus3), .A5(bus4), .A6(bus5), .A7(bus6), .A8(bus7),
    .OE_active_low(not_3_out), .B1(i0), .B2(i1), .B3(i2), .B4(i3), .B5(1'b0), .B6(1'b0), .B7(1'b0),
    .B8(1'b0), .DIR(1'b0));
  not not_3 (not_3_out, in_2);

  // Other names for the same wires on the sheet: clk = in_3; ctrl_IR_in = in_1; ctrl_IR_out = in_2

  // Notes on the sheet:
  //   INSTRUCTION REGISTER
  //   SYSTEM BUS
endmodule

module Output_Register (
  input  in_1,
  input  in_2,
  input  in_3,
  input  [7:0] in_4,
  input  in_5
);

  wire bus0, bus1, bus2, bus3, bus4, bus5, bus6, bus7, ic_74173_quad_d_type_flip_flop_1_q0,
       ic_74173_quad_d_type_flip_flop_1_q1, ic_74173_quad_d_type_flip_flop_1_q2,
       ic_74173_quad_d_type_flip_flop_1_q3, ic_74173_quad_d_type_flip_flop_2_q0,
       ic_74173_quad_d_type_flip_flop_2_q1, ic_74173_quad_d_type_flip_flop_2_q2,
       ic_74173_quad_d_type_flip_flop_2_q3, n74139_1_pin15, n74161_1_pin1, n74161_1_pin2, n74161_1_pin7,
       n74161_1_pin9, n74161_1_pin10, n74161_1_pin13, n74161_1_pin14, not_1_out, not_2_out, Y0, Y1, Y2, Y3;
  wire [2:0] controlled_buffer_2_out, controlled_buffer_4_out, controlled_buffer_6_out,
       controlled_buffer_7_out, ic_cat28c16a_2kx8b_display_1_p20;
  wire [3:0] controlled_buffer_1_out, controlled_buffer_3_out, controlled_buffer_5_out,
       controlled_buffer_8_out, ic_cat28c16a_2kx8b_display_1_p21;

  _74161 #(.ShowInternalStructure("true")) u_74161_1 (
    .pin1(n74161_1_pin1), .pin2(n74161_1_pin2), .pin7(n74161_1_pin7), .pin14(n74161_1_pin14),
    .pin13(n74161_1_pin13), .pin10(n74161_1_pin10), .pin9(n74161_1_pin9));  // open: pin3, pin4, pin5, pin6, pin15, pin12, pin11
  Clock clock_1 (.out(n74161_1_pin2));
  _74139 #(.ShowInternalStructure("true")) u_74139_1 (
    .pin15(n74139_1_pin15), .pin14(n74161_1_pin14), .pin13(n74161_1_pin13), .pin12(Y0), .pin11(Y1),
    .pin10(Y2), .pin9(Y3));  // open: pin1, pin2, pin3, pin4, pin5, pin6, pin7
  IC_74173_quad_D_type_flip_flop ic_74173_quad_d_type_flip_flop_1 (
    .Q0(ic_74173_quad_d_type_flip_flop_1_q0), .Q1(ic_74173_quad_d_type_flip_flop_1_q1),
    .Q2(ic_74173_quad_d_type_flip_flop_1_q2), .Q3(ic_74173_quad_d_type_flip_flop_1_q3),
    .E1_active_low(not_1_out), .E2_active_low(not_1_out), .CP(in_5), .MR(1'b0), .OE1_active_low(1'b0),
    .D0(bus4), .D1(bus5), .D2(bus6), .OE2_active_low(1'b0), .D3(bus7));
  IC_74173_quad_D_type_flip_flop ic_74173_quad_d_type_flip_flop_2 (
    .Q0(ic_74173_quad_d_type_flip_flop_2_q0), .Q1(ic_74173_quad_d_type_flip_flop_2_q1),
    .Q2(ic_74173_quad_d_type_flip_flop_2_q2), .Q3(ic_74173_quad_d_type_flip_flop_2_q3),
    .E1_active_low(not_1_out), .E2_active_low(not_1_out), .CP(in_5), .MR(1'b0), .OE1_active_low(1'b0),
    .D0(bus0), .D1(bus1), .D2(bus2), .OE2_active_low(1'b0), .D3(bus3));
  not not_1 (not_1_out, in_3);
  assign controlled_buffer_1_out = Y3 ? ic_cat28c16a_2kx8b_display_1_p21 : 4'bz;  // Controlled_Buffer controlled_buffer_1
  _7_Segment_Display u_7_segment_display_1 (
    .g(controlled_buffer_1_out[0]), .f(controlled_buffer_1_out[1]), .a(controlled_buffer_1_out[2]),
    .b(controlled_buffer_1_out[3]), .e(controlled_buffer_2_out[2]), .d(controlled_buffer_2_out[1]),
    .c(controlled_buffer_2_out[0]));  // open: dp
  // IC_CAT28C16A_2Kx8b_display ic_cat28c16a_2kx8b_display_1: pin names not known; wires that end beside it: ic_74173_quad_d_type_flip_flop_1_q3, n74161_1_pin14, ic_74173_quad_d_type_flip_flop_1_q2, n74161_1_pin13, ic_74173_quad_d_type_flip_flop_1_q1, 1'b1, ic_74173_quad_d_type_flip_flop_1_q0, 1'b0, ic_74173_quad_d_type_flip_flop_2_q3, in_1, ic_74173_quad_d_type_flip_flop_2_q2, 1'b0, ic_74173_quad_d_type_flip_flop_2_q1, ic_74173_quad_d_type_flip_flop_2_q0, ic_cat28c16a_2kx8b_display_1_p21[3], ic_cat28c16a_2kx8b_display_1_p20[2], ic_cat28c16a_2kx8b_display_1_p21[2], ic_cat28c16a_2kx8b_display_1_p20[1], ic_cat28c16a_2kx8b_display_1_p21[1], ic_cat28c16a_2kx8b_display_1_p20[0], ic_cat28c16a_2kx8b_display_1_p21[0]
  assign controlled_buffer_2_out = Y3 ? ic_cat28c16a_2kx8b_display_1_p20 : 3'bz;  // Controlled_Buffer controlled_buffer_2
  assign controlled_buffer_3_out = Y2 ? ic_cat28c16a_2kx8b_display_1_p21 : 4'bz;  // Controlled_Buffer controlled_buffer_3
  _7_Segment_Display u_7_segment_display_2 (
    .g(controlled_buffer_3_out[0]), .f(controlled_buffer_3_out[1]), .a(controlled_buffer_3_out[2]),
    .b(controlled_buffer_3_out[3]), .e(controlled_buffer_4_out[2]), .d(controlled_buffer_4_out[1]),
    .c(controlled_buffer_4_out[0]));  // open: dp
  assign controlled_buffer_4_out = Y2 ? ic_cat28c16a_2kx8b_display_1_p20 : 3'bz;  // Controlled_Buffer controlled_buffer_4
  assign controlled_buffer_5_out = Y1 ? ic_cat28c16a_2kx8b_display_1_p21 : 4'bz;  // Controlled_Buffer controlled_buffer_5
  _7_Segment_Display u_7_segment_display_3 (
    .g(controlled_buffer_5_out[0]), .f(controlled_buffer_5_out[1]), .a(controlled_buffer_5_out[2]),
    .b(controlled_buffer_5_out[3]), .e(controlled_buffer_6_out[2]), .d(controlled_buffer_6_out[1]),
    .c(controlled_buffer_6_out[0]));  // open: dp
  _7_Segment_Display u_7_segment_display_4 (
    .g(controlled_buffer_8_out[0]), .f(controlled_buffer_8_out[1]), .a(controlled_buffer_8_out[2]),
    .b(controlled_buffer_8_out[3]), .e(controlled_buffer_7_out[2]), .d(controlled_buffer_7_out[1]),
    .c(controlled_buffer_7_out[0]));  // open: dp
  assign controlled_buffer_6_out = Y1 ? ic_cat28c16a_2kx8b_display_1_p20 : 3'bz;  // Controlled_Buffer controlled_buffer_6
  assign controlled_buffer_7_out = Y0 ? ic_cat28c16a_2kx8b_display_1_p20 : 3'bz;  // Controlled_Buffer controlled_buffer_7
  assign controlled_buffer_8_out = Y0 ? ic_cat28c16a_2kx8b_display_1_p21 : 4'bz;  // Controlled_Buffer controlled_buffer_8
  LED led_1 (.in(bus7));
  not not_2 (not_2_out, in_2);
  LED led_2 (.in(bus6));
  LED led_3 (.in(bus5));
  LED led_4 (.in(bus4));
  LED led_5 (.in(bus3));
  LED led_6 (.in(bus2));
  LED led_7 (.in(bus1));
  LED led_8 (.in(bus0));
  IC_74245_octal_transceiver_up ic_74245_octal_transceiver_up_1 (
    .B1(bus7), .B2(bus6), .B3(bus5), .B4(bus4), .B5(bus3), .B6(bus2), .B7(bus1), .B8(bus0),
    .OE_active_low(not_2_out), .A1(in_4[7]), .A2(in_4[6]), .A3(in_4[5]), .A4(in_4[4]), .A5(in_4[3]),
    .DIR(1'b1), .A6(in_4[2]), .A7(in_4[1]), .A8(in_4[0]));
  // also tied to GND on the sheet: n74139_1_pin15
  // also tied to VCC on the sheet: {n74161_1_pin1, n74161_1_pin10, n74161_1_pin7, n74161_1_pin9}

  // Other names for the same wires on the sheet: clk = in_5; ctrl_OR_in = in_3

  // Notes on the sheet:
  //   OUTPUT REGISTER
  //   SYSTEM BUS
endmodule

module IC_74173_quad_D_type_flip_flop (
  input  OE1_active_low,
  input  OE2_active_low,
  input  E1_active_low,
  input  E2_active_low,
  input  CP,
  input  MR,
  input  D0,
  input  D1,
  input  D2,
  input  D3,
  output Q0,
  output Q1,
  output Q2,
  output Q3
);

  wire and_1_out, and_2_out, and_3_out, and_4_out, and_5_out, and_6_out, and_7_out, and_8_out, buffer_1_out,
       buffer_2_out, buffer_3_out, buffer_4_out, buffer_7_out, buffer_8_out, buffer_9_out, buffer_10_out,
       CP_t, d_ff_1_q, d_ff_2_q, d_ff_3_q, d_ff_4_q, E, MR_t, not_E, OE, or_2_out, or_3_out, or_4_out,
       or_5_out;

  buf buffer_1 (buffer_1_out, OE1_active_low);
  buf buffer_2 (buffer_2_out, OE2_active_low);
  buf buffer_3 (buffer_3_out, E1_active_low);
  buf buffer_4 (buffer_4_out, E2_active_low);
  buf buffer_5 (CP_t, CP);
  buf buffer_6 (MR_t, MR);
  buf buffer_7 (buffer_7_out, D0);
  buf buffer_8 (buffer_8_out, D1);
  buf buffer_9 (buffer_9_out, D2);
  buf buffer_10 (buffer_10_out, D3);
  nor nor_1 (OE, buffer_1_out, buffer_2_out);
  or or_1 (E, buffer_3_out, buffer_4_out);
  not not_1 (not_E, E);
  and and_1 (and_1_out, d_ff_1_q, E);
  and and_2 (and_2_out, not_E, buffer_7_out);
  and and_3 (and_3_out, d_ff_2_q, E);
  and and_4 (and_4_out, not_E, buffer_8_out);
  and and_5 (and_5_out, d_ff_3_q, E);
  and and_6 (and_6_out, not_E, buffer_9_out);
  and and_7 (and_7_out, d_ff_4_q, E);
  and and_8 (and_8_out, not_E, buffer_10_out);
  D_Flip_Flop d_ff_1 (.D(or_2_out), .clk(CP_t), .Q(d_ff_1_q), .reset(MR_t));  // open: Qn, preset
  or or_2 (or_2_out, and_1_out, and_2_out);
  D_Flip_Flop d_ff_2 (.D(or_3_out), .clk(CP_t), .Q(d_ff_2_q), .reset(MR_t));  // open: Qn, preset
  or or_3 (or_3_out, and_3_out, and_4_out);
  D_Flip_Flop d_ff_3 (.D(or_4_out), .clk(CP_t), .Q(d_ff_3_q), .reset(MR_t));  // open: Qn, preset
  or or_4 (or_4_out, and_5_out, and_6_out);
  D_Flip_Flop d_ff_4 (.D(or_5_out), .clk(CP_t), .Q(d_ff_4_q), .reset(MR_t));  // open: Qn, preset
  or or_5 (or_5_out, and_7_out, and_8_out);
  assign Q0 = OE ? d_ff_1_q : 1'bz;  // Controlled_Buffer controlled_buffer_1
  assign Q1 = OE ? d_ff_2_q : 1'bz;  // Controlled_Buffer controlled_buffer_2
  assign Q2 = OE ? d_ff_3_q : 1'bz;  // Controlled_Buffer controlled_buffer_3
  assign Q3 = OE ? d_ff_4_q : 1'bz;  // Controlled_Buffer controlled_buffer_4
endmodule

module IC_74245_octal_transceiver_up (
  input  DIR,
  input  OE_active_low,
  input  A1,
  input  A2,
  input  A3,
  input  A4,
  input  A5,
  input  A6,
  input  A7,
  input  A8,
  output B1,
  output B2,
  output B3,
  output B4,
  output B5,
  output B6,
  output B7,
  output B8
);

  wire and_1_out, and_2_out;

  and and_1 (and_1_out, DIR, ~OE_active_low);  // AND_Gate
  assign B1 = and_1_out ? A1 : 1'bz;  // Controlled_Buffer controlled_buffer_1
  assign B2 = and_1_out ? A2 : 1'bz;  // Controlled_Buffer controlled_buffer_2
  assign B3 = and_1_out ? A3 : 1'bz;  // Controlled_Buffer controlled_buffer_3
  assign B4 = and_1_out ? A4 : 1'bz;  // Controlled_Buffer controlled_buffer_4
  assign B5 = and_1_out ? A5 : 1'bz;  // Controlled_Buffer controlled_buffer_5
  assign B6 = and_1_out ? A6 : 1'bz;  // Controlled_Buffer controlled_buffer_6
  assign B7 = and_1_out ? A7 : 1'bz;  // Controlled_Buffer controlled_buffer_7
  assign B8 = and_1_out ? A8 : 1'bz;  // Controlled_Buffer controlled_buffer_8
  and and_2 (and_2_out, ~DIR, ~OE_active_low);  // AND_Gate
  assign A1 = and_2_out ? B1 : 1'bz;  // Controlled_Buffer controlled_buffer_9
  assign A2 = and_2_out ? B2 : 1'bz;  // Controlled_Buffer controlled_buffer_10
  assign A3 = and_2_out ? B3 : 1'bz;  // Controlled_Buffer controlled_buffer_11
  assign A4 = and_2_out ? B4 : 1'bz;  // Controlled_Buffer controlled_buffer_12
  assign A5 = and_2_out ? B5 : 1'bz;  // Controlled_Buffer controlled_buffer_13
  assign A6 = and_2_out ? B6 : 1'bz;  // Controlled_Buffer controlled_buffer_14
  assign A7 = and_2_out ? B7 : 1'bz;  // Controlled_Buffer controlled_buffer_15
  assign A8 = and_2_out ? B8 : 1'bz;  // Controlled_Buffer controlled_buffer_16
endmodule

module IC_74245_octal_transceiver_down (
  input  DIR,
  input  OE_active_low,
  input  B1,
  input  B2,
  input  B3,
  input  B4,
  input  B5,
  input  B6,
  input  B7,
  input  B8,
  output A1,
  output A2,
  output A3,
  output A4,
  output A5,
  output A6,
  output A7,
  output A8
);

  wire and_1_out, and_2_out;

  and and_1 (and_1_out, DIR, ~OE_active_low);  // AND_Gate
  assign B1 = and_1_out ? A1 : 1'bz;  // Controlled_Buffer controlled_buffer_1
  assign B2 = and_1_out ? A2 : 1'bz;  // Controlled_Buffer controlled_buffer_2
  assign B3 = and_1_out ? A3 : 1'bz;  // Controlled_Buffer controlled_buffer_3
  assign B4 = and_1_out ? A4 : 1'bz;  // Controlled_Buffer controlled_buffer_4
  assign B5 = and_1_out ? A5 : 1'bz;  // Controlled_Buffer controlled_buffer_5
  assign B6 = and_1_out ? A6 : 1'bz;  // Controlled_Buffer controlled_buffer_6
  assign B7 = and_1_out ? A7 : 1'bz;  // Controlled_Buffer controlled_buffer_7
  assign B8 = and_1_out ? A8 : 1'bz;  // Controlled_Buffer controlled_buffer_8
  and and_2 (and_2_out, ~DIR, ~OE_active_low);  // AND_Gate
  assign A1 = and_2_out ? B1 : 1'bz;  // Controlled_Buffer controlled_buffer_9
  assign A2 = and_2_out ? B2 : 1'bz;  // Controlled_Buffer controlled_buffer_10
  assign A3 = and_2_out ? B3 : 1'bz;  // Controlled_Buffer controlled_buffer_11
  assign A4 = and_2_out ? B4 : 1'bz;  // Controlled_Buffer controlled_buffer_12
  assign A5 = and_2_out ? B5 : 1'bz;  // Controlled_Buffer controlled_buffer_13
  assign A6 = and_2_out ? B6 : 1'bz;  // Controlled_Buffer controlled_buffer_14
  assign A7 = and_2_out ? B7 : 1'bz;  // Controlled_Buffer controlled_buffer_15
  assign A8 = and_2_out ? B8 : 1'bz;  // Controlled_Buffer controlled_buffer_16
endmodule

module IC_74189 (
  input  A0,
  input  D1,
  input  D2,
  input  A1,
  input  D3,
  input  D4,
  input  A2,
  input  WE_not,
  input  A3,
  output S1_not,
  output S2_not,
  output S3_not,
  output S4_not
);

  wire and_1_out, and_2_out, and_3_out, and_4_out, and_5_out, and_6_out, and_7_out, and_8_out, and_9_out,
       and_10_out, and_11_out, and_12_out, and_13_out, and_14_out, and_15_out, and_16_out, not_A0, not_A1,
       not_A2, not_A3, S1, S2, S3, S4, WE;

  and and_1 (and_1_out, not_A0, not_A1, not_A2, not_A3);
  and and_2 (and_2_out, A0, not_A1, not_A2, not_A3);
  and and_3 (and_3_out, not_A0, A1, not_A2, not_A3);
  and and_4 (and_4_out, A0, A1, not_A2, not_A3);
  and and_5 (and_5_out, not_A0, not_A1, A2, not_A3);
  and and_6 (and_6_out, A0, not_A1, A2, not_A3);
  and and_7 (and_7_out, not_A0, A1, A2, not_A3);
  and and_8 (and_8_out, A0, A1, A2, not_A3);
  not not_1 (not_A0, A0);
  not not_2 (not_A1, A1);
  not not_3 (not_A2, A2);
  not not_4 (not_A3, A3);
  not not_5 (WE, WE_not);
  memory_cell_4_bit memory_cell_4_bit_1 (
    .Q1(S2), .Q2(S3), .Q3(S4), .Q0(S1), .D1(D2), .D2(D3), .D3(D4), .selected(and_1_out), .WE(WE), .D0(D1));
  memory_cell_4_bit memory_cell_4_bit_2 (
    .Q1(S2), .Q2(S3), .Q3(S4), .Q0(S1), .D1(D2), .D2(D3), .D3(D4), .selected(and_2_out), .WE(WE), .D0(D1));
  memory_cell_4_bit memory_cell_4_bit_3 (
    .Q1(S2), .Q2(S3), .Q3(S4), .Q0(S1), .D1(D2), .D2(D3), .D3(D4), .selected(and_3_out), .WE(WE), .D0(D1));
  memory_cell_4_bit memory_cell_4_bit_4 (
    .Q1(S2), .Q2(S3), .Q3(S4), .Q0(S1), .D1(D2), .D2(D3), .D3(D4), .selected(and_4_out), .WE(WE), .D0(D1));
  memory_cell_4_bit memory_cell_4_bit_5 (
    .Q1(S2), .Q2(S3), .Q3(S4), .Q0(S1), .D1(D2), .D2(D3), .D3(D4), .selected(and_5_out), .WE(WE), .D0(D1));
  memory_cell_4_bit memory_cell_4_bit_6 (
    .Q1(S2), .Q2(S3), .Q3(S4), .Q0(S1), .D1(D2), .D2(D3), .D3(D4), .selected(and_6_out), .WE(WE), .D0(D1));
  memory_cell_4_bit memory_cell_4_bit_7 (
    .Q1(S2), .Q2(S3), .Q3(S4), .Q0(S1), .D1(D2), .D2(D3), .D3(D4), .selected(and_7_out), .WE(WE), .D0(D1));
  memory_cell_4_bit memory_cell_4_bit_8 (
    .Q1(S2), .Q2(S3), .Q3(S4), .Q0(S1), .D1(D2), .D2(D3), .D3(D4), .selected(and_8_out), .WE(WE), .D0(D1));
  not not_6 (S1_not, S1);
  not not_7 (S2_not, S2);
  not not_8 (S3_not, S3);
  not not_9 (S4_not, S4);
  and and_9 (and_9_out, not_A0, not_A1, not_A2, A3);
  and and_10 (and_10_out, A0, not_A1, not_A2, A3);
  and and_11 (and_11_out, not_A0, A1, not_A2, A3);
  and and_12 (and_12_out, A0, A1, not_A2, A3);
  and and_13 (and_13_out, not_A0, not_A1, A2, A3);
  and and_14 (and_14_out, A0, not_A1, A2, A3);
  and and_15 (and_15_out, not_A0, A1, A2, A3);
  and and_16 (and_16_out, A0, A1, A2, A3);
  memory_cell_4_bit memory_cell_4_bit_9 (
    .Q1(S2), .Q2(S3), .Q3(S4), .Q0(S1), .D1(D2), .D2(D3), .D3(D4), .selected(and_9_out), .WE(WE), .D0(D1));
  memory_cell_4_bit memory_cell_4_bit_10 (
    .Q1(S2), .Q2(S3), .Q3(S4), .Q0(S1), .D1(D2), .D2(D3), .D3(D4), .selected(and_10_out), .WE(WE), .D0(D1));
  memory_cell_4_bit memory_cell_4_bit_11 (
    .Q1(S2), .Q2(S3), .Q3(S4), .Q0(S1), .D1(D2), .D2(D3), .D3(D4), .selected(and_11_out), .WE(WE), .D0(D1));
  memory_cell_4_bit memory_cell_4_bit_12 (
    .Q1(S2), .Q2(S3), .Q3(S4), .Q0(S1), .D1(D2), .D2(D3), .D3(D4), .selected(and_12_out), .WE(WE), .D0(D1));
  memory_cell_4_bit memory_cell_4_bit_13 (
    .Q1(S2), .Q2(S3), .Q3(S4), .Q0(S1), .D1(D2), .D2(D3), .D3(D4), .selected(and_13_out), .WE(WE), .D0(D1));
  memory_cell_4_bit memory_cell_4_bit_14 (
    .Q1(S2), .Q2(S3), .Q3(S4), .Q0(S1), .D1(D2), .D2(D3), .D3(D4), .selected(and_14_out), .WE(WE), .D0(D1));
  memory_cell_4_bit memory_cell_4_bit_15 (
    .Q1(S2), .Q2(S3), .Q3(S4), .Q0(S1), .D1(D2), .D2(D3), .D3(D4), .selected(and_15_out), .WE(WE), .D0(D1));
  memory_cell_4_bit memory_cell_4_bit_16 (
    .Q1(S2), .Q2(S3), .Q3(S4), .Q0(S1), .D1(D2), .D2(D3), .D3(D4), .selected(and_16_out), .WE(WE), .D0(D1));
endmodule

module IC_CAT28C16A_2Kx8b_display (
  input  A0,
  input  A1,
  input  A2,
  input  A3,
  input  A4,
  input  A5,
  input  A6,
  input  A7,
  input  A8,
  input  A9,
  input  A10,
  output Q0,
  output Q1,
  output Q2,
  output Q3,
  output Q4,
  output Q5,
  output Q6,
  output Q7
);

  ROM #(.addrWidth(11)) rom_1 (
    .addr({A10, A9, A8, A7, A6, A5, A4, A3, A2, A1, A0}), .data({Q7, Q6, Q5, Q4, Q3, Q2, Q1, Q0}));

  // Notes on the sheet:
  //   contents of rom_1 (hex, n*v repeats v):
  //   77 41 6e 6b 59 3b 3f 61 7f 7b 77 41 6e 6b 59 3b 3f 61 7f 7b 77 41 6e 6b 59 3b 3f 61 7f 7b 77 41 6e
  //   6b 59 3b 3f 61 7f 7b 77 41 6e 6b 59 3b 3f 61 7f 7b 77 41 6e 6b 59 3b 3f 61 7f 7b 77 41 6e 6b 59 3b
  //   3f 61 7f 7b 77 41 6e 6b 59 3b 3f 61 7f 7b 77 41 6e 6b 59 3b 3f 61 7f 7b 77 41 6e 6b 59 3b 3f 61 7f
  //   7b 77 41 6e 6b 59 3b 3f 61 7f 7b 77 41 6e 6b 59 3b 3f 61 7f 7b 77 41 6e 6b 59 3b 3f 61 7f 7b 77 41
  //   6e 6b 59 3b 3f 61 7f 7b 77 41 6e 6b 59 3b 3f 61 7f 7b 77 41 6e 6b 59 3b 3f 61 7f 7b 77 41 6e 6b 59
  //   3b 3f 61 7f 7b 77 41 6e 6b 59 3b 3f 61 7f 7b 77 41 6e 6b 59 3b 3f 61 7f 7b 77 41 6e 6b 59 3b 3f 61
  //   7f 7b 77 41 6e 6b 59 3b 3f 61 7f 7b 77 41 6e 6b 59 3b 3f 61 7f 7b 77 41 6e 6b 59 3b 3f 61 7f 7b 77
  //   41 6e 6b 59 3b 3f 61 7f 7b 77 41 6e 6b 59 3b 3f 61 7f 7b 77 41 6e 6b 59 3b 10*77 10*41 10*6e 10*6b
  //   10*59 10*3b 10*3f 10*61 10*7f 10*7b 10*77 10*41 10*6e 10*6b 10*59 10*3b 10*3f 10*61 10*7f 10*7b
  //   10*77 10*41 10*6e 10*6b 10*59 6*3b 100*77 100*41 56*6e 256*0 77 41 6e 6b 59 3b 3f 61 7f 7b 77 41 6e
  //   6b 59 3b 3f 61 7f 7b 77 41 6e 6b 59 3b 3f 61 7f 7b 77 41 6e 6b 59 3b 3f 61 7f 7b 77 41 6e 6b 59 3b
  //   3f 61 7f 7b 77 41 6e 6b 59 3b 3f 61 7f 7b 77 41 6e 6b 59 3b 3f 61 7f 7b 77 41 6e 6b 59 3b 3f 61 7f
  //   7b 77 41 6e 6b 59 3b 3f 61 7f 7b 77 41 6e 6b 59 3b 3f 61 7f 7b 77 41 6e 6b 59 3b 3f 61 7f 7b 77 41
  //   6e 6b 59 3b 3f 61 7f 7b 77 41 6e 6b 59 3b 3f 61 7f 61 3f 3b 59 6b 6e 41 77 7b 7f 61 3f 3b 59 6b 6e
  //   41 77 7b 7f 61 3f 3b 59 6b 6e 41 77 7b 7f 61 3f 3b 59 6b 6e 41 77 7b 7f 61 3f 3b 59 6b 6e 41 77 7b
  //   7f 61 3f 3b 59 6b 6e 41 77 7b 7f 61 3f 3b 59 6b 6e 41 77 7b 7f 61 3f 3b 59 6b 6e 41 77 7b 7f 61 3f
  //   3b 59 6b 6e 41 77 7b 7f 61 3f 3b 59 6b 6e 41 77 7b 7f 61 3f 3b 59 6b 6e 41 77 7b 7f 61 3f 3b 59 6b
  //   6e 41 77 7b 7f 61 3f 3b 59 6b 6e 41 10*77 10*41 10*6e 10*6b 10*59 10*3b 10*3f 10*61 10*7f 10*7b
  //   10*77 10*41 17*6e 10*41 10*77 10*7b 10*7f 10*61 10*3f 10*3b 10*59 10*6b 10*6e 10*41 109*77 57*41
  //   99*77 128*0 128*8
endmodule

module SR_latch_active_low (
  input  S,
  input  R,
  output Q,
  output not_Q
);

  nand nand_1 (Q, S, not_Q);
  nand nand_2 (not_Q, Q, R);
endmodule

module memory_1_bit (
  input  input_value,
  input  set,
  output output_value
);

  wire nand_1_out, nand_2_out;

  nand nand_1 (nand_1_out, input_value, set);
  nand nand_2 (nand_2_out, nand_1_out, set);
  SR_latch_active_low sr_latch_active_low_1 (.Q(output_value), .R(nand_2_out), .S(nand_1_out));  // open: not_Q
endmodule

module memory_cell_4_bit (
  input  D0,
  input  D1,
  input  D2,
  input  D3,
  input  selected,
  input  WE,
  output Q0,
  output Q1,
  output Q2,
  output Q3
);

  wire memory_1_bit_1_output_value, memory_1_bit_2_output_value, memory_1_bit_3_output_value,
       memory_1_bit_4_output_value, WE_t;

  memory_1_bit memory_1_bit_1 (.output_value(memory_1_bit_1_output_value), .set(WE_t), .input_value(D0));
  memory_1_bit memory_1_bit_2 (.output_value(memory_1_bit_2_output_value), .set(WE_t), .input_value(D1));
  memory_1_bit memory_1_bit_3 (.output_value(memory_1_bit_3_output_value), .set(WE_t), .input_value(D2));
  memory_1_bit memory_1_bit_4 (.output_value(memory_1_bit_4_output_value), .set(WE_t), .input_value(D3));
  and and_1 (WE_t, WE, selected);
  assign Q0 = selected ? memory_1_bit_1_output_value : 1'bz;  // Controlled_Buffer controlled_buffer_1
  assign Q1 = selected ? memory_1_bit_2_output_value : 1'bz;  // Controlled_Buffer controlled_buffer_2
  assign Q2 = selected ? memory_1_bit_3_output_value : 1'bz;  // Controlled_Buffer controlled_buffer_3
  assign Q3 = selected ? memory_1_bit_4_output_value : 1'bz;  // Controlled_Buffer controlled_buffer_4
endmodule
